// Logisim project PROJECT.circ as structural Verilog: 4 circuits, main circuit main
module main (
  input  [3:0] in_1
);

  wire CLK_out, OUTR_p3;
  wire [3:0] AC_p3, alu_4_1_out_14, AR_p1, AR_p3, controlled_buffer_1_out, DR_p3, PC_p3, undriven,
       undriven_2, undriven_3, undriven_4;
  wire [7:0] IR_output, ram_1_data;

  ALU_4 alu_4_1 (
    .AC(AC_p3), .DR(DR_p3), .INPR(in_1), .out_14(alu_4_1_out_14));  // open: AND, ADD, CMA, LD_DR, LD_INPR, CIR, CIL, Cin, Cout, E_AC_0, E_AC_3
  Clock CLK (.out(CLK_out));
  RAM #(.addrWidth(4), .bus("separate")) ram_1 (
    .addr(AR_p3), .din({controlled_buffer_1_out, AR_p1}), .data(ram_1_data), .clk(CLK_out));  // open: str, sel, ld, clr
  // _4_REG AR: pin names not known; wires that end beside it: AR_p1, CLK_out, AR_p3
  // Probe on undriven
  // _4_REG PC: pin names not known; wires that end beside it: AR_p1, CLK_out, PC_p3
  // _4_REG DR: pin names not known; wires that end beside it: AR_p1, CLK_out, DR_p3
  // _4_REG AC: pin names not known; wires that end beside it: alu_4_1_out_14, CLK_out, AC_p3
  _8_REG IR (.in_1({controlled_buffer_1_out, AR_p1}), .LD(CLK_out), .OUTPUT(IR_output));  // open: CLK
  // Probe on OUTR_p3
  // _4_REG OUTR: pin names not known; wires that end beside it: AR_p1, CLK_out, OUTR_p3
  Controlled_Buffer #(.width(8)) controlled_buffer_1 (
    .in(ram_1_data), .out({controlled_buffer_1_out, AR_p1}));  // open: en
  Controlled_Buffer #(.width(8)) controlled_buffer_2 (
    .in({undriven, AR_p3}), .out({controlled_buffer_1_out, AR_p1}));  // open: en
  Controlled_Buffer #(.width(8)) controlled_buffer_3 (
    .in({undriven_2, PC_p3}), .out({controlled_buffer_1_out, AR_p1}));  // open: en
  Controlled_Buffer #(.width(8)) controlled_buffer_4 (
    .in({undriven_3, DR_p3}), .out({controlled_buffer_1_out, AR_p1}));  // open: en
  Controlled_Buffer #(.width(8)) controlled_buffer_5 (
    .in({undriven_4, AC_p3}), .out({controlled_buffer_1_out, AR_p1}));  // open: en
  Controlled_Buffer #(.width(8)) controlled_buffer_6 (
    .in(IR_output), .out({controlled_buffer_1_out, AR_p1}));  // open: en
endmodule

module _8_REG (
  input  [7:0] in_1,
  input  CLK,
  input  LD,
  output [7:0] OUTPUT
);

  // _4_REG 4_reg_1: pin names not known; wires that end beside it: in_1[3:0], CLK, LD, OUTPUT[3:0]
  // _4_REG 4_reg_2: pin names not known; wires that end beside it: in_1[7:4], CLK, LD, OUTPUT[7:4]
endmodule

module AC (
  input  INPR,
  input  DR,
  input  AC,
  input  AND,
  input  Cin,
  input  ADD,
  input  CMA,
  input  LD_DR,
  input  LD_INPR,
  input  CIR,
  input  AC_0_1,
  input  CIL,
  input  AC_0_1_2,
  output Cout,
  output OUTPUT_AC
);

  wire adder_1_out, and_1_out, and_2_out, and_3_out, and_4_out, and_5_out, and_6_out, and_7_out, not_1_out;

  Adder #(.width(1)) adder_1 (.a(AC), .b(DR), .out(adder_1_out), .cin(Cin), .cout(Cout));
  not not_1 (not_1_out, AC);
  and and_1 (and_1_out, AND, AC, DR);
  and and_2 (and_2_out, ADD, adder_1_out);
  and and_3 (and_3_out, CMA, not_1_out);
  and and_4 (and_4_out, LD_DR, DR);
  and and_5 (and_5_out, LD_INPR, INPR);
  and and_6 (and_6_out, CIR, AC_0_1);
  and and_7 (and_7_out, CIL, AC_0_1_2);
  or or_1 (OUTPUT_AC, and_1_out, and_2_out, and_3_out, and_4_out, and_5_out, and_6_out, and_7_out);
endmodule

module ALU_4 (
  input  Cin,
  input  [3:0] AC,
  input  [3:0] DR,
  input  E_AC_0,
  input  [3:0] INPR,
  input  AND,
  input  ADD,
  input  CMA,
  input  LD_DR,
  input  LD_INPR,
  input  CIR,
  input  CIL,
  input  E_AC_3,
  output [3:0] out_14,
  output Cout
);

  wire ac_1_cout, ac_2_cout, ac_3_cout;

  AC ac_1 (
    .AND(AND), .ADD(ADD), .CMA(CMA), .LD_DR(LD_DR), .LD_INPR(LD_INPR), .CIR(CIR), .AC_0_1(CIL), .CIL(E_AC_0),
    .AC_0_1_2(AC[1]), .INPR(INPR[0]), .DR(DR[0]), .AC(AC[0]), .Cin(Cin), .Cout(ac_1_cout),
    .OUTPUT_AC(out_14[0]));
  AC ac_2 (
    .AND(AND), .ADD(ADD), .CMA(CMA), .LD_DR(LD_DR), .LD_INPR(LD_INPR), .CIR(CIR), .AC_0_1(CIL), .CIL(AC[0]),
    .AC_0_1_2(AC[2]), .INPR(INPR[1]), .DR(DR[1]), .AC(AC[1]), .Cin(ac_1_cout), .Cout(ac_2_cout),
    .OUTPUT_AC(out_14[1]));
  AC ac_3 (
    .AND(AND), .ADD(ADD), .CMA(CMA), .LD_DR(LD_DR), .LD_INPR(LD_INPR), .CIR(CIR), .AC_0_1(CIL), .CIL(AC[1]),
    .AC_0_1_2(AC[3]), .INPR(INPR[2]), .DR(DR[2]), .AC(AC[2]), .Cin(ac_2_cout), .Cout(ac_3_cout),
    .OUTPUT_AC(out_14[2]));
  AC ac_4 (
    .AND(AND), .ADD(ADD), .CMA(CMA), .LD_DR(LD_DR), .LD_INPR(LD_INPR), .CIR(CIR), .AC_0_1(CIL), .CIL(AC[2]),
    .AC_0_1_2(E_AC_3), .INPR(INPR[3]), .DR(DR[3]), .AC(AC[3]), .Cin(ac_3_cout), .Cout(Cout),
    .OUTPUT_AC(out_14[3]));
endmodule
